// Logisim project 000_Decoder.circ as structural Verilog: 2 circuits, main circuit main
module main (
  input  x2,
  input  x1,
  input  [1:0] in_3,
  input  Enable,
  input  [1:0] Input,
  output y1,
  output y2,
  output y3,
  output y4,
  output [3:0] out_10,
  output [3:0] Output
);

  wire not_1_out, not_2_out, not_3_out, not_4_out;

  not not_1 (not_1_out, x2);
  not not_2 (not_2_out, x1);
  and and_1 (out_10[0], not_3_out, not_4_out);
  and and_2 (out_10[1], not_3_out, in_3[0]);
  and and_3 (out_10[2], in_3[1], not_4_out);
  and and_4 (out_10[3], in_3[1], in_3[0]);
  not not_3 (not_3_out, in_3[1]);
  not not_4 (not_4_out, in_3[0]);
  and and_5 (y1, not_1_out, not_2_out);
  and and_6 (y2, not_1_out, x1);
  and and_7 (y3, x2, not_2_out);
  and and_8 (y4, x2, x1);
  Decoder #(.select(2)) decoder_1 (
    .out0(Output[0]), .out1(Output[1]), .out2(Output[2]), .out3(Output[3]), .sel(Input), .en(Enable));

  // Notes on the sheet:
  //   2-bit Decoder
  //   Using a Bus
  //   Individual Inputs
  //   y1=(x1)' * (x2)'
  //   y2=x1 * (x2)'
  //   y3=(x1)' * x2
  //   y4=x1 * x2
endmodule

module _2_bit_Decoder (
  input  x1,
  input  x2,
  output y1,
  output y2,
  output y3,
  output y4
);

  wire not_1_out, not_2_out, not_3_out, not_4_out;

  not not_1 (not_1_out, x1);
  not not_2 (not_2_out, x2);
  not not_3 (not_3_out, x1);
  not not_4 (not_4_out, x2);
  and and_1 (y4, x1, x2);
  and and_2 (y1, not_1_out, not_2_out);
  and and_3 (y2, not_3_out, x2);
  and and_4 (y3, x1, not_4_out);
endmodule
