// Logisim project 000_Decoder_and_MUX.circ as structural Verilog: 1 circuit, main circuit main
module main (
  input  in_1,
  input  in_2,
  input  in_3,
  input  in_4,
  input  in_5,
  input  in_6,
  input  in_7,
  input  in_8,
  input  in_9,
  input  in_10,
  input  in_11,
  output out_12,
  output out_13,
  output out_14,
  output out_15,
  output out_16,
  output out_17,
  output out_18,
  output out_19
);

  wire and_5_out, and_6_out, and_7_out, and_8_out, clock_1_out, not_1_out, not_2_out, not_3_out, not_4_out;

  Clock clock_1 (.out(clock_1_out));
  D_Flip_Flop d_ff_1 (.clk(in_9), .D(in_10), .Q(out_17));  // open: Qn, preset, en, reset
  D_Flip_Flop d_ff_2 (.clk(clock_1_out), .D(in_11), .Q(out_18));  // open: Qn, preset, en, reset
  not not_1 (not_1_out, in_6);
  not not_2 (not_2_out, in_5);
  D_Flip_Flop d_ff_3 (.clk(clock_1_out), .D(in_11), .Q(out_19));  // open: Qn, preset, en, reset
  and and_1 (out_12, not_2_out, not_1_out);
  and and_2 (out_13, not_2_out, in_6);
  and and_3 (out_14, in_5, not_1_out);
  and and_4 (out_16, in_5, in_6);
  and and_5 (and_5_out, in_1, not_3_out, not_4_out);
  and and_6 (and_6_out, in_2, not_3_out, in_8);
  and and_7 (and_7_out, in_3, in_7, not_4_out);
  and and_8 (and_8_out, in_4, in_7, in_8);
  not not_3 (not_3_out, in_7);
  not not_4 (not_4_out, in_8);
  or or_1 (out_15, and_5_out, and_6_out, and_7_out, and_8_out);

  // Notes on the sheet:
  //   2-bit Decoder
  //   4x1 MUX
endmodule
